# Fritzing sketch Test_water_sensor (saved by Fritzing 0.9.6b)

parts:
  Test_water_level = Water Level Sensor
  WeMos_D1_Mini1 = WeMos D1 Mini

nets:
  N1: Test_water_level.SIG, WeMos_D1_Mini1.A0
  N2: Test_water_level.VCC, WeMos_D1_Mini1.D1
  N3: Test_water_level.GND, WeMos_D1_Mini1.G

custom parts:
  Water Level Sensor: A water level sensor. This sensor operates at 3V to 5V. The Sig (signal) pin outputs an analogue signal that is in proportion to the amount of water in contact with the sensor.
